# Fritzing sketch arduino_rover (saved by Fritzing 0.9.3b)
circuit board: 8.46667cm x 5.64444cm
breadboards: 1

parts:
  Part1 = Arduino Uno (Rev3)
  IR1 = TSOP312.., 314.. [package=THT]
  LED1 = LEDs [package=led10mm]
  M1 = DC Motor
  M2 = DC Motor
  IC1 = L293D [package=THT]
  VCC1 = 4 x AAA Battery Mount  # not connected
  R1 = Resistor [tolerance=±5% resistance=220 package=THT]  # not connected

nets (from the schematic view):
  N1: Part1.D8, IC1.In_4
  GND: Part1.GND, IR1.GND, LED1.C, IC1.0V
  N2: Part1.D3_PWM, IR1.Data
  N3: Part1.D5_PWM, IC1.In_1
  N4: Part1.D6_PWM, IC1.In_3
  N5: Part1.D7, IC1.In_2
  N6: Part1.5V, IR1.Vs, IC1.Enable_1, IC1.+Vmotor, IC1.Enable_2, IC1.+V
  N7: M1.pin_1, IC1.Out_3_(_Controlled_by_Enable_2_)
  N8: M1.pin_2, IC1.Out_4_(_Controlled_by_Enable_2_)
  N9: M2.pin_1, IC1.Out_1_(_Controlled_by_Enable_1_)
  N10: M2.pin_2, IC1.Out_2_(_Controlled_by_Enable_1_)
